// Logisim project AVX_project.circ as structural Verilog
module main (
  input  in_1,
  input  in_2,
  output out_3
);

  CLA_Adder cla_adder_1 (.A(in_1), .B(in_2), .Sum(out_3));
endmodule

// VHDL entity AVX, as the project stores it:
--------------------------------------------------------------------------------
-- Project : AVX 
-- File    : --
-- Autor   : Alexandre Chiacchio e Nayara Gomes
-- Date    : 28 de Setembro de 2023
--
--------------------------------------------------------------------------------
-- Description : Somador/Subtrator Vetorial de 32 bits
--
--------------------------------------------------------------------------------

LIBRARY ieee;
USE ieee.std_logic_1164.all;

ENTITY AVX IS
  PORT (
  ------------------------------------------------------------------------------
  -- Entradas
   	A_i        	: IN  std_logic_vector(31 DOWNTO 0); 	-- Operando A
    	B_i        	: IN  std_logic_vector(31 DOWNTO 0); 	-- Operando B
    	mode_i 		: IN  std_logic; 					-- Modo de operação
    	vecSize_i 	: IN  std_logic_vector(1 DOWNTO 0); 	-- Tamanho do Vetor
    	
  ------------------------------------------------------------------------------
  -- Saídas
     S_o        	: OUT std_logic_vector(31 DOWNTO 0)     
  );
END AVX;

--------------------------------------------------------------------------------
-- Arquitetura
--------------------------------------------------------------------------------

ARCHITECTURE TypeArchitecture OF AVX IS

signal B_s 	: std_logic_vector(31 DOWNTO 0);

signal w_C 	: std_logic_vector(31 DOWNTO 0);
signal w_G 	: std_logic_vector(31 DOWNTO 0);
signal w_P 	: std_logic_vector(31 DOWNTO 0);

signal w_SUM  	: std_logic_vector(31 DOWNTO 0);

BEGIN

-- Caso seja uma subtração, inverte-se o valor de B
B_s <= B_i WHEN (mode_i = '0') ELSE 
	 NOT(B_i) WHEN (mode_i = '1');


--Gera-se o carry de Geração (G) e de Propagação (P) para o carry lookahead
GEN_CLA : FOR ii IN 0 TO 31 generate
    w_G(ii) <= A_i(ii) AND B_s(ii);
    w_P(ii) <= A_i(ii) OR B_s(ii);
  
END generate GEN_CLA;
 
 
-- Realizamos as somas para chegar ao resultado final
  GEN_ADDER : FOR jj IN 0 TO 31 generate
    w_SUM (jj) <= A_i(jj) XOR B_s(jj);
  END generate GEN_ADDER;


  S_o <= w_SUM;


END TypeArchitecture;

// VHDL entity CLA_Adder, as the project stores it:
library IEEE;
use IEEE.STD_LOGIC_1164.ALL;
use IEEE.STD_LOGIC_ARITH.ALL;
use IEEE.STD_LOGIC_UNSIGNED.ALL;

entity CLA_Adder is
    Port (
        A, B : in  STD_LOGIC;

        Sum  : out STD_LOGIC
    );
end CLA_Adder;

architecture Behavioral of CLA_Adder is
begin
    
    Sum <= A AND B;
end Behavioral;
